// Logisim project CoreARM_Revision1.circ as structural Verilog: 3 circuits, main circuit CoreARM
module CoreARM (
);

  ALU ArithmeticLogicUnit ();  // open: Control, A, B, Subtract, Cin, Result, N, C, Z, V
endmodule

module RegisterFile (
  input  [3:0] ReadReg1,
  input  [3:0] WriteReg,
  input  [31:0] WriteData,
  input  RegWrite,
  input  Clock,
  input  [3:0] ReadReg2,
  output [31:0] ReadData1,
  output [31:0] ReadData2
);

  wire decoder_1_p3, decoder_1_p4, decoder_1_p5, decoder_1_p6, decoder_1_p7, decoder_1_p8, decoder_1_p9,
       decoder_1_p10, decoder_1_p11, decoder_1_p12, decoder_1_p13, decoder_1_p14, decoder_1_p15,
       decoder_1_p16, decoder_1_p17, decoder_1_p18;
  wire [31:0] R7_q, R15_q;

  // Decoder #(.enable("true"), .select(4)) decoder_1: pin names not known; wires that end beside it: WriteReg, RegWrite, decoder_1_p3, decoder_1_p4, decoder_1_p5, decoder_1_p6, decoder_1_p7, decoder_1_p8, decoder_1_p9, decoder_1_p10, decoder_1_p11, decoder_1_p12, decoder_1_p13, decoder_1_p14, decoder_1_p15, decoder_1_p16, decoder_1_p17, decoder_1_p18
  // Register #(.width(32)) R0: pin names not known; wires that end beside it: WriteData, decoder_1_p3, Clock, WriteData
  Register #(.width(32)) R8 (.D(WriteData), .en(decoder_1_p11), .clk(Clock), .Q(WriteData));  // open: clr
  // Register #(.width(32)) R1: pin names not known; wires that end beside it: WriteData, decoder_1_p4, Clock, WriteData
  Register #(.width(32)) R9 (.D(WriteData), .en(decoder_1_p12), .clk(Clock), .Q(WriteData));  // open: clr
  // Register #(.width(32)) R2: pin names not known; wires that end beside it: WriteData, decoder_1_p5, Clock, WriteData
  Register #(.width(32)) R10 (.D(WriteData), .en(decoder_1_p13), .clk(Clock), .Q(WriteData));  // open: clr
  // Register #(.width(32)) R3: pin names not known; wires that end beside it: WriteData, decoder_1_p6, Clock, WriteData
  Register #(.width(32)) R11 (.D(WriteData), .en(decoder_1_p14), .clk(Clock), .Q(WriteData));  // open: clr
  // Register #(.width(32)) R4: pin names not known; wires that end beside it: WriteData, decoder_1_p7, Clock, WriteData
  Register #(.width(32)) R12 (.D(WriteData), .en(decoder_1_p15), .clk(Clock), .Q(WriteData));  // open: clr
  Register #(.width(32)) R5 (.D(WriteData), .en(decoder_1_p8), .clk(Clock), .Q(WriteData));  // open: clr
  Register #(.width(32)) R13 (.D(WriteData), .en(decoder_1_p16), .clk(Clock), .Q(WriteData));  // open: clr
  Register #(.width(32)) R6 (.D(WriteData), .en(decoder_1_p9), .clk(Clock), .Q(WriteData));  // open: clr
  Register #(.width(32)) R14 (.D(WriteData), .en(decoder_1_p17), .clk(Clock), .Q(WriteData));  // open: clr
  Register #(.width(32)) R7 (.D(WriteData), .en(decoder_1_p10), .clk(Clock), .Q(R7_q));  // open: clr
  Register #(.width(32)) R15 (.D(WriteData), .en(decoder_1_p18), .clk(Clock), .Q(R15_q));  // open: clr
  Multiplexer #(.select(4), .width(32)) multiplexer_1 (
    .in0(WriteData), .in1(WriteData), .in2(WriteData), .in3(WriteData), .in4(WriteData), .in5(WriteData),
    .in6(WriteData), .in7(R7_q), .in8(WriteData), .in9(WriteData), .in10(WriteData), .in11(WriteData),
    .in12(WriteData), .in13(WriteData), .in14(WriteData), .in15(R15_q), .out(ReadData1), .sel(ReadReg1));
  Multiplexer #(.select(4), .width(32)) multiplexer_2 (
    .in0(WriteData), .in1(WriteData), .in2(WriteData), .in3(WriteData), .in4(WriteData), .in5(WriteData),
    .in6(WriteData), .in7(R7_q), .in8(WriteData), .in9(WriteData), .in10(WriteData), .in11(WriteData),
    .in12(WriteData), .in13(WriteData), .in14(WriteData), .in15(R15_q), .out(ReadData2), .sel(ReadReg2));
endmodule

module ALU (
  input  [2:0] Control,
  input  [31:0] A,
  input  [31:0] B,
  input  Subtract,
  input  Cin,
  output [31:0] Result,
  output N,
  output C,
  output Z,
  output V
);

  wire or_1_out, or_3_out;
  wire [31:0] adder_1_out, and_1_out, bit_extender_1_out, or_2_out, xor_1_out, xor_2_out;

  assign bit_extender_1_out = {{31{Subtract}}, Subtract};  // Bit_Extender bit_extender_1
  assign xor_1_out = B ^ bit_extender_1_out;  // XOR_Gate xor_1, 32 bits wide
  or or_1 (or_1_out, Subtract, Cin);
  assign and_1_out = A & B;  // AND_Gate and_1, 32 bits wide
  assign or_2_out = A | B;  // OR_Gate or_2, 32 bits wide
  assign xor_2_out = A ^ B;  // XOR_Gate xor_2, 32 bits wide
  Adder #(.width(32)) adder_1 (.a(A), .b(xor_1_out), .out(adder_1_out), .cin(or_1_out), .cout(C));
  xor xor_3 (V, or_1_out, C);
  Multiplexer #(.select(3), .width(32)) multiplexer_1 (
    .in0(adder_1_out), .in1(adder_1_out), .in2(and_1_out), .in3(or_2_out), .in4(xor_2_out),
    .out({N, Result[30:7], Result[7], Result[5:0]}), .sel(Control));  // open: in5, in6, in7
  or or_3 (or_3_out, N, Result[30], Result[29], Result[28], Result[27], Result[26], Result[25], Result[24], Result[23], Result[22], Result[21], Result[20], Result[19], Result[18], Result[17], Result[16], Result[15], Result[14], Result[13], Result[12], Result[11], Result[10], Result[9], Result[8], Result[7], Result[7], Result[5], Result[4], Result[3], Result[2], Result[1], Result[0]);
  not not_1 (Z, or_3_out);

  assign {Result[31], Result[6]} = {N, Result[7]};
endmodule
