// Logisim project CoreASM_Revision1.circ as structural Verilog: 2 circuits, main circuit CoreARM
module CoreARM (
);

  ALU ArithmeticLogicUnit ();  // open: Control, A, B, Subtract, Cin, Result, N, C, Z, V
endmodule

module ALU (
  input  [2:0] Control,
  input  [31:0] A,
  input  [31:0] B,
  input  Subtract,
  input  Cin,
  output [31:0] Result,
  output N,
  output C,
  output Z,
  output V
);

  wire or_1_out, or_3_out;
  wire [31:0] adder_1_out, and_1_out, bit_extender_1_out, or_2_out, xor_1_out, xor_2_out;

  assign bit_extender_1_out = {{31{Subtract}}, Subtract};  // Bit_Extender bit_extender_1
  assign xor_1_out = B ^ bit_extender_1_out;  // XOR_Gate xor_1, 32 bits wide
  or or_1 (or_1_out, Subtract, Cin);
  assign and_1_out = A & B;  // AND_Gate and_1, 32 bits wide
  assign or_2_out = A | B;  // OR_Gate or_2, 32 bits wide
  assign xor_2_out = A ^ B;  // XOR_Gate xor_2, 32 bits wide
  Adder #(.width(32)) adder_1 (.a(A), .b(xor_1_out), .out(adder_1_out), .cin(or_1_out), .cout(C));
  xor xor_3 (V, or_1_out, C);
  Multiplexer #(.select(3), .width(32)) multiplexer_1 (
    .in0(adder_1_out), .in1(adder_1_out), .in2(and_1_out), .in3(or_2_out), .in4(xor_2_out),
    .out({N, Result[30:7], Result[7], Result[5:0]}), .sel(Control));  // open: in5, in6, in7
  or or_3 (or_3_out, N, Result[30], Result[29], Result[28], Result[27], Result[26], Result[25], Result[24], Result[23], Result[22], Result[21], Result[20], Result[19], Result[18], Result[17], Result[16], Result[15], Result[14], Result[13], Result[12], Result[11], Result[10], Result[9], Result[8], Result[7], Result[7], Result[5], Result[4], Result[3], Result[2], Result[1], Result[0]);
  not not_1 (Z, or_3_out);

  assign {Result[31], Result[6]} = {N, Result[7]};
endmodule
